# Fritzing sketch Struct_Class_Abfrage (saved by Fritzing 0.9.10b)

parts:
  Bauteil1 = Arduino Uno (Rev3)
  Bauteil2 = LCD1602-I2C
  Keypad4x1 = Keypad Membran 4x4

nets:
  N1: Bauteil1.D8, Keypad4x1.Pin2
  N2: Bauteil1.D9_PWM, Keypad4x1.Pin1
  GND: Bauteil1.GND, Bauteil2.GND
  N3: Bauteil1.A4/SDA, Bauteil2.SDA
  N4: Bauteil1.A5/SCL, Bauteil2.SCL
  N5: Bauteil1.D2, Keypad4x1.Pin8
  N6: Bauteil1.D3_PWM, Keypad4x1.Pin7
  N7: Bauteil1.D4, Keypad4x1.Pin6
  N8: Bauteil1.D5_PWM, Keypad4x1.Pin5
  N9: Bauteil1.D6_PWM, Keypad4x1.Pin4
  N10: Bauteil1.D7, Keypad4x1.Pin3
  5V: Bauteil1.5V, Bauteil2.VCC

notes:
  Struct & Class Abfrage

custom parts:
  LCD1602-I2C: A standard character display, usually with 2x16 characters. Comes in many colors with LCM1602 IIC attached.
  Keypad Membran 4x4: Membrane Keypad 4x4 Matrix
